# Fritzing sketch aquarium (saved by Fritzing 0.9.1b)
circuit board: 8.46667cm x 5.64444cm
breadboards: 1

parts:
  Tiny_RTC = Tiny RTC
  S5 = Pushbutton [package="[THT]"]
  S4 = Pushbutton [package="[THT]"]
  S3 = Pushbutton [package="[THT]"]
  S2 = Pushbutton [package="[THT]"]
  S1 = Pushbutton [package="[THT]"]
  R5 = Resistor [tolerance=±5% resistance=2.2k package=THT]
  R4 = Resistor [tolerance=±5% resistance=1k package=THT]
  R3 = Resistor [tolerance=±5% resistance=680 package=THT]
  R2 = Resistor [tolerance=±5% resistance=330 package=THT]
  R1 = Resistor [tolerance=±5% resistance=2k package=THT]
  LED1 = LED - 5mm [color="Red (633nm)" package="5 mm [THT]"]
  LED2 = LED - 5mm [color="Yellow (585nm)" package="5 mm [THT]"]
  LED3 = LED - 5mm [color="Green (555nm)" package="5 mm [THT]"]
  LED4 = LED - 5mm [color="Blue (470nm)" package="5 mm [THT]"]
  R11 = Resistor [tolerance=±5% resistance=220 package=THT]
  R12 = Resistor [tolerance=±5% resistance=220 package=THT]
  R13 = Resistor [tolerance=±5% resistance=220 package=THT]
  R14 = Resistor [tolerance=±5% resistance=220 package=THT]
  LED5 = LED - 5mm [color="Green (570nm)" package="5 mm [THT]"]
  R15 = Resistor [tolerance=±5% resistance=220 package=THT]
  J1_-_18V = Power Jack [package=power_jack_smd]
  Power_LED9 = Power LED on star
  Power_LED4 = Power LED on star
  Power_LED1 = Power LED on star
  Power_LED7 = Power LED on star
  Power_LED6 = Power LED on star
  Power_LED3 = Power LED on star
  Power_LED5 = Power LED on star
  Power_LED2 = Power LED on star
  Power_LED8 = Power LED on star
  ProMini_5V = Arduino Pro Mini v13
  WF_S1 = WaterFlow hall effect sensor
  DS1 = DS18B20 1-Wire Temperature Sensor [part_number=DS18B20]
  7-35V_to_5V = QSKJ DC-DC stepdown converter
  I2C_LCD1 = LCD screen witch I2C connector
  LDD-1000H1 = MeanWell LDD-1000H
  LDD-1000H2 = MeanWell LDD-1000H
  FTDI_USB/Serial1 = FTDI Basic Programmer
  R6 = Resistor [tolerance=±5% resistance=4.7k package=THT]
  R7 = Resistor [tolerance=±5% resistance=10k package=THT]
  LED6 = LED - 5mm [color="Red (633nm)" package="5 mm [THT]"]
  R16 = Resistor [tolerance=±5% resistance=220 package=THT]
  4_Relay_Module1 = 4 Relay Module

nets:
  N1: Tiny_RTC.SCL, ProMini_5V.A5, I2C_LCD1.SCL
  N2: Tiny_RTC.SDA, ProMini_5V.A4, I2C_LCD1.SDA
  5V: Tiny_RTC.VCC, R1.Pin_0, ProMini_5V.VCC, WF_S1.VDD, DS1.VDD, 7-35V_to_5V.OUT+, I2C_LCD1.VCC, R6.Pin_1, R7.Pin_1, 4_Relay_Module1.VCC, 4_Relay_Module1.JD-VCC
  GND: Tiny_RTC.GND, S5.Pin_1, S5.Pin_2, S4.Pin_1, S4.Pin_2, S3.Pin_1, S3.Pin_2, S2.Pin_1, S2.Pin_2, S1.Pin_1, S1.Pin_2, R11.Pin_0, R12.Pin_0, R13.Pin_0, R14.Pin_0, R15.Pin_0, ProMini_5V.GND, WF_S1.GND, DS1.GND, 7-35V_to_5V.OUT-, I2C_LCD1.GND, FTDI_USB/Serial1.GND, R16.Pin_0, 4_Relay_Module1.GND
  N3: S5.Pin_3, S5.Pin_4, R5.Pin_1
  N4: S4.Pin_3, S4.Pin_4, R5.Pin_0, R4.Pin_1
  N5: S3.Pin_3, S3.Pin_4, R4.Pin_0, R3.Pin_1
  N6: S2.Pin_3, S2.Pin_4, R3.Pin_0, R2.Pin_1
  N7: S1.Pin_3, S1.Pin_4, R2.Pin_0, R1.Pin_1, ProMini_5V.A1
  N8: LED1.cathode, R11.Pin_1
  Light_1: LED1.anode, ProMini_5V.D10_PWM/SS, LDD-1000H1.PWM_DIM
  N9: LED2.cathode, R12.Pin_1
  Light_2: LED2.anode, ProMini_5V.D11_PWM/MOSI, LDD-1000H2.PWM_DIM
  N10: LED3.cathode, R13.Pin_1
  Switch_1: LED3.anode, ProMini_5V.D9_PWM, 4_Relay_Module1.IN1
  N11: LED4.cathode, R14.Pin_1
  Switch_2: LED4.anode, ProMini_5V.D8, 4_Relay_Module1.IN2
  N12: LED5.cathode, R15.Pin_1
  Switch_3: LED5.anode, ProMini_5V.D7, 4_Relay_Module1.IN3
  N13: J1_-_18V.PWR, 7-35V_to_5V.IN+, LDD-1000H1.+Vin, LDD-1000H2.+Vin
  N14: J1_-_18V.GND, 7-35V_to_5V.IN-, LDD-1000H1.-Vin, LDD-1000H2.-Vin
  N15: Power_LED9.+, Power_LED8.-
  N16: Power_LED9.-, LDD-1000H2.-Vout
  N17: Power_LED4.+, Power_LED3.-
  N18: Power_LED4.-, LDD-1000H1.-Vout
  N19: Power_LED1.+, LDD-1000H1.+Vout
  N20: Power_LED1.-, Power_LED2.+
  N21: Power_LED7.+, Power_LED6.-
  N22: Power_LED7.-, Power_LED8.+
  N23: Power_LED6.+, Power_LED5.-
  N24: Power_LED3.+, Power_LED2.-
  N25: Power_LED5.+, LDD-1000H2.+Vout
  N26: ProMini_5V.DTR, FTDI_USB/Serial1.DTR
  N27: ProMini_5V.D0/TX, FTDI_USB/Serial1.RXI
  N28: ProMini_5V.D1/RX, FTDI_USB/Serial1.TXO
  Switch_4: ProMini_5V.D6_PWM, LED6.anode, 4_Relay_Module1.IN4
  N29: ProMini_5V.D4, DS1.DQ, R6.Pin_0
  N30: ProMini_5V.D2, WF_S1.SIG, R7.Pin_0
  N31: LED6.cathode, R16.Pin_1

notes:
  Light_1
  Light_2
  Switch_1
  Switch_2

custom parts:
  Tiny RTC: Tiny RTC I2C module DS1370Z RTC and AT24C32 EEPROM
  Power LED on star: PCB mounted RGB LED.
  DS18B20 1-Wire Temperature Sensor: DS18B20 1-Wire Temperature Sensor - waterproof version
  QSKJ DC-DC stepdown converter: Description: This is a 2A stepdown converter - Brand: Jtron - Model: 03100125 - Color: Red - Material: Glass fiber - Module properties: Non-isolated step-down module (Buck) - Rectification: Non-synchronous - Input voltage: DC 4.5~35V - Output voltage: 1.25~30V (adjustable or fixed) - Rated current: 2A - Output current: Max. 3A; Suggest add heat sink if output power is over 15W - Conversion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
  LCD screen witch I2C connector: A standard character display with I2C interface, usually with 2x16 characters. Comes in many colors.
  MeanWell LDD-1000H: DC-DC Constant Current Step-Down LED drive
  4 Relay Module: a 4 relay module for Arduino or other
